# Fritzing sketch schematic (saved by Fritzing 0.9.10b)
breadboards: 1

parts:
  Part2 = Arduino Nano (Rev3.0)
  DATA_0 = female pin header, 1 pin [form="♀ (female)"]
  Squix1 = OLED 0.96" 128x64 I2C SSD1306
  DATA_1 = female pin header, 1 pin [form="♀ (female)"]
  DATA_2 = female pin header, 1 pin [form="♀ (female)"]
  DATA_3 = female pin header, 1 pin [form="♀ (female)"]
  DATA_4 = female pin header, 1 pin [form="♀ (female)"]
  DATA_5 = female pin header, 1 pin [form="♀ (female)"]
  DATA_6 = female pin header, 1 pin [form="♀ (female)"]
  DATA_7 = female pin header, 1 pin [form="♀ (female)"]
  ADDR_0 = female pin header, 1 pin [form="♀ (female)"]
  ADDR_1 = female pin header, 1 pin [form="♀ (female)"]
  ENABLE = female pin header, 1 pin [form="♀ (female)"]
  INTERRUPT = female pin header, 1 pin [form="♀ (female)"]

nets:
  GND: Part2.GND, Squix1.GND
  N1: Part2.D2, INTERRUPT.pin1
  N2: Part2.D3, ENABLE.pin1
  N3: Part2.D4, DATA_0.pin1
  N4: Part2.D5, DATA_1.pin1
  N5: Part2.D6, DATA_2.pin1
  N6: Part2.D7, DATA_3.pin1
  N7: Part2.D8, DATA_4.pin1
  N8: Part2.D9, DATA_5.pin1
  N9: Part2.D10, DATA_6.pin1
  N10: Part2.D11/MOSI, DATA_7.pin1
  5V: Part2.5V, Squix1.VCC
  N11: Part2.A5, Squix1.SCL
  N12: Part2.A4, Squix1.SCA
  N13: Part2.A1, ADDR_1.pin1
  N14: Part2.A0, ADDR_0.pin1
